# Fritzing sketch drone_circuit (saved by Fritzing 0.9.1b)
circuit board: 9.5cm x 9.5cm
breadboards: 1

parts:
  M2 = DC Motor
  M3 = DC Motor
  JP2 = Header 2 [package=jst-2-pth-kit]
  M4 = DC Motor
  Part1 = Arduino Pro Mini v13
  GY2 = MPU-6050 Board GY-521 [form="♀ (female)" package=THT]
  Q1 = NPN-Transistor [package="TO92 [THT]"]
  M5 = DC Motor
  Q2 = NPN-Transistor [package="TO92 [THT]"]
  Q3 = NPN-Transistor [package="TO92 [THT]"]
  Q4 = NPN-Transistor [package="TO92 [THT]"]
  C1 = Capacitor [package=cap-pth-small-kit]
  part = DC Motor  # not connected
  D1 = Diode [package=diode-1n4001]
  D4 = Diode [package=diode-1n4001]
  D3 = Diode [package=diode-1n4001]
  D2 = Diode [package=diode-1n4001]

nets (from the pcb view):
  N1: M2.pin_1, M3.pin_2, JP2.1, M4.pin_1, Part1.VCC, GY2.pin1, M5.pin_2, C1.1, D1.C, D4.C, D3.C, D2.A
  N2: M2.pin_2, Q3.C, D2.C
  N3: M3.pin_1, Q2.E, D1.A
  N4: JP2.2, Part1.GND, GY2.pin2, Q1.E, Q2.C, Q3.E, Q4.E, C1.2
  N5: M4.pin_2, Q4.C, D4.A
  N6: Part1.A3, GY2.pin3
  N7: Part1.A2, GY2.pin4
  N8: Part1.D10_PWM/SS, Q2.B
  N9: Part1.D9_PWM, Q3.B
  N10: Part1.D5_PWM, Q4.B
  N11: Part1.D4, GY2.pin8
  N12: Part1.D3_PWM, Q1.B
  N13: Q1.C, M5.pin_1, D3.A

custom parts:
  MPU-6050 Board GY-521: Acelerometro y Giroscopio MPU-6050 Board GY-521
